# Fritzing sketch RFID_reader (saved by Fritzing 0.9.2b)
breadboards: 1

parts:
  Part1 = RFID-RC522-v2
  Part2 = Adafruit Breadboard-Friendly NeoPixel [part_number="Adafruit #1312"]
  WeMos_D1_Mini1 = WeMos D1 Mini
  S1 = Pushbutton [package="[THT]"]
  Part4 = VERTER 5V USB Buck-Boost
  C1 = Ceramic Capacitor [capacitance=100nF package="100 mil [THT, multilayer]"]
  C2 = Electrolytic Capacitor [capacitance=100µF package="100 mil [THT, electrolytic]"]

nets:
  N1: Part1.SDA, WeMos_D1_Mini1.D8
  N2: Part1.SCK, WeMos_D1_Mini1.D5
  N3: Part1.MOSI, WeMos_D1_Mini1.D7
  N4: Part1.MISO, WeMos_D1_Mini1.D6
  GND: Part1.GND, Part2.GND, WeMos_D1_Mini1.G, S1.Pin_1, S1.Pin_2, Part4.GND, C1.1, C2.-
  N5: Part1.RST, WeMos_D1_Mini1.D4
  3.3V: Part1.3.3V, WeMos_D1_Mini1.3V3
  N6: Part2.IN, WeMos_D1_Mini1.D1
  5V: Part2.VDD, WeMos_D1_Mini1.5V, Part4.5.0V, C2.+
  N7: WeMos_D1_Mini1.D3, S1.Pin_3, S1.Pin_4, C1.0

notes:
  +5V
  +3V
  Wemos no use pins: D0, D3, D2
  12V in

custom parts:
  RFID-RC522-v2: A simple China made RFID-RC522 Reader; do check the pin labels, as this is a MFRC522 based clone.
  Adafruit Breadboard-Friendly NeoPixel: This is the easiest way possible to add small, bright RGB pixels to your project. We took the same technology from our Flora NeoPixels and made them breadboard friendly, with two rows of 3 x 0.1" spaced header on each side for easy soldering, chaining and breadboarding. These ultra-bright LEDs have a constant-current driver cooked right into the LED package! The pixels are chainable - so you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
  WeMos D1 Mini: The D1 mini is a mini wifi board based on ESP-8266EX.
  VERTER 5V USB Buck-Boost: VERTER can take battery voltages from 3-12VDC and output a nice 5V DC, which makes it a perfect universal power supply for your portable project! Where Verter really shines is when you have a battery or power range that can fluctuate a lot, or you don't know what you'll end up using.
